# Fritzing sketch Rotary Actuator (saved by Fritzing 0.9.6b)

parts:
  Motor_Driver = L9110 H-bridge module [part_number="L9110 H-bridge"]
  부품1 = Arduino Uno (Rev3)
  A1 = Rotary Actuator  # not connected

nets:
  GND: Motor_Driver.GND, 부품1.GND
  VCC: Motor_Driver.VCC, 부품1.5V
  N1: Motor_Driver.A-IA, 부품1.D9_PWM
  N2: Motor_Driver.A-IB, 부품1.D8

custom parts:
  Rotary Actuator: Rotary Actuator using Clock Actuator
